# Fritzing sketch dht22 (saved by Fritzing 0.9.2b)
breadboards: 1

parts:
  Composant1 = Arduino Nano (Rev3.0)
  RHT1 = Humidity and Temperature Sensor RHT03

nets:
  N1: Composant1.GND, RHT1.GND_2
  N2: Composant1.D11/MOSI, RHT1.Data-signal
  5V: Composant1.5V, RHT1.Vcc
